# Fritzing sketch safelab (saved by Fritzing 0.9.3b)
breadboards: 1

parts:
  J1 = Piezo Speaker
  GSM_SIM_GPSR_SMS_SIM900_SIM1 = SIM800L [package=THT]
  Grove1 = Grove OLED 128x96
  U1 = GAS_SENSOR [package=mq-3]
  DHT1 = DHT11 Humitidy and Temperature Sensor
  Componente1 = Arduino Uno (Rev3) - ICSP
  U2 = LIPO-2000mAh [package=lipo-2000]

nets:
  GND: J1.pin1, Grove1.GND, U1.A1, DHT1.GND, Componente1.GND
  N1: J1.pin2, Componente1.D7
  N2: GSM_SIM_GPSR_SMS_SIM900_SIM1.5V, U2.+
  N3: GSM_SIM_GPSR_SMS_SIM900_SIM1.GND, U2.-
  N4: GSM_SIM_GPSR_SMS_SIM900_SIM1.SIM_TXD, Componente1.D3_PWM
  N5: GSM_SIM_GPSR_SMS_SIM900_SIM1.SIM_RXD, Componente1.D4
  VCC: Grove1.VCC, U1.B1, DHT1.VDD, Componente1.5V
  N6: Grove1.SDA, Componente1.A4/SDA
  N7: Grove1.SCL, Componente1.A5/SCL
  N8: DHT1.DATA, Componente1.A1

custom parts:
  DHT11 Humitidy and Temperature Sensor: DHT11 Humidity and Temperature Sensor
